// Logisim project cpu.circ as structural Verilog: 2 circuits, main circuit CPU
module CPU (
  input  [31:0] Instruction,
  input  CLK,
  output [31:0] s0,
  output [31:0] s1,
  output [31:0] t0,
  output [31:0] t1,
  output [31:0] a0,
  output [31:0] ra,
  output [31:0] sp,
  output [31:0] PC
);

  wire comparator_1_eq, comparator_2_eq, comparator_3_eq, comparator_4_eq, comparator_5_eq, comparator_6_eq,
       comparator_7_eq, comparator_8_eq, or_1_out, or_2_out, WE;
  wire [2:0] and_1_out, and_2_out, and_3_out, and_4_out, and_5_out, bit_extender_5_out, bit_extender_6_out,
       bit_extender_7_out, bit_extender_8_out, bit_extender_9_out, SEL;
  wire [31:0] IMM, multiplexer_2_out, regfile_1_r1, regfile_1_r2, TIPO_B, TIPO_I, TIPO_J, TIPO_S;

  // Incrementer incrementer_1: pin names not known
  Multiplexer #(.select(3), .width(32), .enable("false")) multiplexer_1 (
    .in1(TIPO_I), .in2(TIPO_S), .in3(TIPO_B), .in4({Instruction[31:12], {12{1'b0}}}), .in5(TIPO_J),
    .out(IMM), .sel(SEL));  // open: in0, in6, in7
  // PC pc_1: pin names not known
  RegFile regfile_1 (
    .Clk(CLK), .R1(regfile_1_r1), .R2(regfile_1_r2), .WE(WE), .RD(Instruction[11:7]),
    .RS1(Instruction[19:15]), .RS2(Instruction[24:20]), .s0(s0), .s1(s1), .t0(t0), .t1(t1), .a0(a0), .ra(ra),
    .sp(sp));  // open: W
  Multiplexer #(.width(32), .enable("false")) multiplexer_2 (
    .in0(regfile_1_r2), .in1(IMM), .out(multiplexer_2_out));  // open: sel
  assign TIPO_I = {{20{Instruction[31]}}, Instruction[31:20]};  // Bit_Extender bit_extender_1
  assign TIPO_S = {{20{Instruction[31]}}, {Instruction[31:25], Instruction[11:7]}};  // Bit_Extender bit_extender_2
  assign TIPO_B = {{19{Instruction[31]}}, {Instruction[31], Instruction[7], Instruction[30:25], Instruction[11:8], 1'b0}};  // Bit_Extender bit_extender_3
  assign TIPO_J = {{11{Instruction[31]}}, {Instruction[31], Instruction[19:12], Instruction[20], Instruction[30:21], 1'b0}};  // Bit_Extender bit_extender_4
  ALU alu_1 (.A(regfile_1_r1), .B(multiplexer_2_out));  // open: ALU_Op, Out
  Comparator #(.width(7), .mode("unsigned")) comparator_1 (
    .a(Instruction[6:0]), .b(7'b0000011), .eq(comparator_1_eq));  // open: gt, lt
  Comparator #(.width(7), .mode("unsigned")) comparator_2 (
    .a(Instruction[6:0]), .b(7'b0010011), .eq(comparator_2_eq));  // open: gt, lt
  Comparator #(.width(7), .mode("unsigned")) comparator_3 (
    .a(Instruction[6:0]), .b(7'b1100111), .eq(comparator_3_eq));  // open: gt, lt
  Comparator #(.width(7), .mode("unsigned")) comparator_4 (
    .a(Instruction[6:0]), .b(7'b0100011), .eq(comparator_4_eq));  // open: gt, lt
  Comparator #(.width(7), .mode("unsigned")) comparator_5 (
    .a(Instruction[6:0]), .b(7'b1100011), .eq(comparator_5_eq));  // open: gt, lt
  Comparator #(.width(7), .mode("unsigned")) comparator_6 (
    .a(Instruction[6:0]), .b(7'b0110111), .eq(comparator_6_eq));  // open: gt, lt
  Comparator #(.width(7), .mode("unsigned")) comparator_7 (
    .a(Instruction[6:0]), .b(7'b0010111), .eq(comparator_7_eq));  // open: gt, lt
  Comparator #(.width(7), .mode("unsigned")) comparator_8 (
    .a(Instruction[6:0]), .b(7'b1101111), .eq(comparator_8_eq));  // open: gt, lt
  or or_1 (or_1_out, comparator_1_eq, comparator_2_eq, comparator_3_eq);
  or or_2 (or_2_out, comparator_6_eq, comparator_7_eq);
  // memory_main main_1: pin names not known
  assign bit_extender_5_out = {{2{1'b1}}, or_1_out};  // Bit_Extender bit_extender_5
  assign bit_extender_6_out = {{2{1'b1}}, comparator_4_eq};  // Bit_Extender bit_extender_6
  assign bit_extender_7_out = {{2{1'b1}}, comparator_5_eq};  // Bit_Extender bit_extender_7
  assign bit_extender_8_out = {{2{1'b1}}, or_2_out};  // Bit_Extender bit_extender_8
  assign bit_extender_9_out = {{2{1'b1}}, comparator_8_eq};  // Bit_Extender bit_extender_9
  assign and_1_out = bit_extender_5_out & 3'b001;  // AND_Gate and_1, 3 bits wide
  assign and_2_out = bit_extender_6_out & 3'b010;  // AND_Gate and_2, 3 bits wide
  assign and_3_out = bit_extender_7_out & 3'b011;  // AND_Gate and_3, 3 bits wide
  assign and_4_out = bit_extender_8_out & 3'b100;  // AND_Gate and_4, 3 bits wide
  assign and_5_out = bit_extender_9_out & 3'b101;  // AND_Gate and_5, 3 bits wide
  assign SEL = and_1_out | and_2_out | and_3_out | and_4_out | and_5_out;  // OR_Gate or_3, 3 bits wide

  // Other names for the same wires on the sheet: INST[31:0] = Instruction; RD[4:0] = Instruction[11:7];
  //   RS2[4:0] = Instruction[24:20]; TIPO_U[31:12] = Instruction[31:12]; F7[6:0] = Instruction[31:25];
  //   F3[2:0] = Instruction[14:12]; RS1[4:0] = Instruction[19:15]; fetch_addr[31:0] = PC;
  //   OPCODE[6:0] = Instruction[6:0]

  // Notes on the sheet:
  //   NOTE
  //   Please do not modify/replace/move/change/delete/etc input and output pins
  //   These are debug/test outputs from your circuit
endmodule

module ImmPeligroso (
  input  [31:0] INST,
  input  [6:0] OPCODE,
  output [31:0] IMM
);

  wire comparator_1_eq, comparator_2_eq, comparator_3_eq, comparator_4_eq, comparator_5_eq, comparator_6_eq,
       or_1_out, or_2_out;
  wire [2:0] SEL;
  wire [31:0] TIPO_B, TIPO_I, TIPO_J, TIPO_S;

  // Probe on INST
  assign TIPO_I = {{20{INST[11]}}, INST[11:0]};  // Bit_Extender bit_extender_1
  assign TIPO_S = {{20{INST[6]}}, {INST[6:0], INST[24:20]}};  // Bit_Extender bit_extender_2
  assign TIPO_B = {{19{INST[0]}}, {INST[0], INST[24], INST[6:1], INST[23:20], 1'b0}};  // Bit_Extender bit_extender_3
  assign TIPO_J = {{11{INST[0]}}, {INST[0], INST[19:1], 1'b0}};  // Bit_Extender bit_extender_4
  Multiplexer #(.select(3), .width(32), .enable("false")) multiplexer_1 (
    .in0(TIPO_I), .in1(TIPO_S), .in2(TIPO_B), .in3({INST[19:0], {12{1'b0}}}), .in4(TIPO_J), .sel(SEL));  // open: in5, in6, in7, out
  Comparator #(.width(7), .mode("unsigned")) comparator_1 (
    .a(OPCODE), .b(7'b0000011), .eq(comparator_1_eq));  // open: gt, lt
  Comparator #(.width(7), .mode("unsigned")) comparator_2 (
    .a(OPCODE), .b(7'b0010011), .eq(comparator_2_eq));  // open: gt, lt
  Comparator #(.width(7), .mode("unsigned")) comparator_3 (
    .a(OPCODE), .b(7'b1100111), .eq(comparator_3_eq));  // open: gt, lt
  or or_1 (or_1_out, comparator_1_eq, comparator_2_eq, comparator_3_eq);
  assign SEL = {{2{1'b0}}, or_1_out};  // Bit_Extender bit_extender_5
  Comparator #(.width(7), .mode("unsigned")) comparator_4 (
    .a(OPCODE), .b(7'b0000011), .eq(comparator_4_eq));  // open: gt, lt
  Comparator #(.width(7), .mode("unsigned")) comparator_5 (
    .a(OPCODE), .b(7'b0010011), .eq(comparator_5_eq));  // open: gt, lt
  Comparator #(.width(7), .mode("unsigned")) comparator_6 (
    .a(OPCODE), .b(7'b1100111), .eq(comparator_6_eq));  // open: gt, lt
  or or_2 (or_2_out, comparator_4_eq, comparator_5_eq, comparator_6_eq);
  assign SEL = {{2{1'b0}}, or_2_out};  // Bit_Extender bit_extender_6

  // Other names for the same wires on the sheet: TIPO_U[31:12] = INST[19:0]
endmodule
